# Fritzing sketch CRA (saved by Fritzing 0.9.3b)
breadboards: 1

parts:
  Accelerometer = Triple Axis Accelerometer Breakout - ADXL345
  Raspberry_Pi_4_Model_B = Raspberry Pi 3 [part_number=RPI-3-V1.2]
  R1 = Resistor [tolerance=±5% resistance=220 package="1206 [SMD]"]
  R2 = Resistor [tolerance=±5% resistance=1.2k package="2512 [SMD]"]
  LED1 = smd LED [color="Red (633nm)" package="0805 [SMD]"]
  R3 = Resistor [tolerance=±5% resistance=220 package="1206 [SMD]"]
  LED2 = smd LED [color="Red (633nm)" package="0805 [SMD]"]
  LED3 = smd LED [color="Red (633nm)" package="0805 [SMD]"]
  LED4 = smd LED [color="Red (633nm)" package="0805 [SMD]"]
  LED5 = smd LED [color="Red (633nm)" package="0805 [SMD]"]
  R4 = Resistor [tolerance=±5% resistance=220 package="1206 [SMD]"]
  R5 = Resistor [tolerance=±5% resistance=220 package="1206 [SMD]"]
  R6 = Resistor [tolerance=±5% resistance=220 package="1206 [SMD]"]
  R7 = Resistor [tolerance=±5% resistance=220 package="1206 [SMD]"]
  Ultrasonic_Sensor = hc-sr04

nets:
  GND: Accelerometer.GND, Raspberry_Pi_4_Model_B.GND, R3.Pin_1, R4.Pin_1, R5.Pin_1, R6.Pin_1, R7.Pin_1, Ultrasonic_Sensor.GND
  VCC: Accelerometer.VCC, Raspberry_Pi_4_Model_B.3v3, Ultrasonic_Sensor.VCC
  N1: Accelerometer.SDA, Raspberry_Pi_4_Model_B.GPIO2
  N2: Accelerometer.SCL, Raspberry_Pi_4_Model_B.GPIO3
  N3: Raspberry_Pi_4_Model_B.GIPO17, LED1.anode
  N4: Raspberry_Pi_4_Model_B.GIPO27, LED5.anode
  N5: Raspberry_Pi_4_Model_B.GIPO22, LED2.anode
  N6: Raspberry_Pi_4_Model_B.GIPO25, LED3.anode
  N7: Raspberry_Pi_4_Model_B.GIPO24, R1.Pin_0, R2.Pin_0
  N8: Raspberry_Pi_4_Model_B.GIPO23, LED4.anode
  N9: Raspberry_Pi_4_Model_B.GIPO18, Ultrasonic_Sensor.Trig
  N10: R1.Pin_1, Ultrasonic_Sensor.Echo
  N11: LED1.cathode, R3.Pin_0
  N12: LED2.cathode, R4.Pin_0
  N13: LED3.cathode, R5.Pin_0
  N14: LED4.cathode, R6.Pin_0
  N15: LED5.cathode, R7.Pin_0
