# Fritzing sketch CRA (saved by Fritzing 0.9.4)

parts:
  S1 = Round Pushbutton [part_number="Power Off"]
  S2 = Round Pushbutton [part_number=Record]
  S3 = Round Pushbutton [part_number="Power On"]
  Raspberry_Pi_4_Model_B = Raspberry Pi 3 [part_number=RPI-3-V1.2]
  TF-Luna_Lidar = tf-luna lidar
  ADX345_Accelerometer = Triple Axis Accelerometer Breakout - ADXL345
  NeoPixel_Stick = NeoPixel Stick [part_number=1426]

nets:
  GND: S1.leg0, S2.leg0, S3.leg0, Raspberry_Pi_4_Model_B.GND, TF-Luna_Lidar.Pin_4, ADX345_Accelerometer.GND, NeoPixel_Stick.GND
  N1: S1.leg1, Raspberry_Pi_4_Model_B.GIPO16
  N2: S2.leg1, Raspberry_Pi_4_Model_B.GIPO21
  N3: S3.leg1, Raspberry_Pi_4_Model_B.GPIO3, ADX345_Accelerometer.SCL
  3V3: Raspberry_Pi_4_Model_B.3v3, ADX345_Accelerometer.VCC
  N4: Raspberry_Pi_4_Model_B.GPIO2, ADX345_Accelerometer.SDA
  N5: Raspberry_Pi_4_Model_B.GIPO18, NeoPixel_Stick.DATAIN
  N6: Raspberry_Pi_4_Model_B.GIPO15, TF-Luna_Lidar.Pin_3
  N7: Raspberry_Pi_4_Model_B.GIPO14, TF-Luna_Lidar.Pin_2
  5V: Raspberry_Pi_4_Model_B.5V, TF-Luna_Lidar.Pin_1, NeoPixel_Stick.+5V

custom parts:
  tf-luna lidar: TF-Luna is using Time of Flight (TOF) principle to measure distance, and it periodically emits near infrared modulated wave.
  NeoPixel Stick: Make your own little LED strip arrangement with this stick of NeoPixel LEDs. We crammed 8 of the tiny 5050 (5mm x 5mm) smart RGB LEDs onto a PCB with mounting holes and a chainable design. Use only one microcontroller pin to control as many as you can chain together! Each LED is addressable as the driver chip is inside the LED. Each one has ~18mA constant current drive so the color will be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
